// Logisim project CPU.circ as structural Verilog: 11 circuits, main circuit main
module main (
  input  in_1,
  input  in_2,
  input  in_3,
  input  in_4,
  input  in_5,
  input  in_6,
  input  in_7,
  input  in_8,
  input  in_9,
  input  in_10,
  input  in_11,
  input  in_12,
  input  in_13,
  input  in_14,
  input  in_15,
  input  in_16,
  input  in_17,
  input  in_18,
  input  in_19,
  input  in_20,
  input  in_21,
  input  in_22,
  input  in_23,
  input  in_24,
  input  in_25
);

  wire AH_out_7, AH_out_8, AH_out_9, AH_out_10, AL_out_7, AL_out_8, AL_out_9, AL_out_10, BH_out_7, BH_out_8,
       BH_out_9, BH_out_10, BL_out_7, BL_out_8, BL_out_9, BL_out_10, CLK_out, IR_out_7, IR_out_8, IR_out_9,
       IR_out_10;

  Clock CLK (.out(CLK_out));
  fourbitregister AL (
    .I1(in_1), .I2(in_2), .I3(in_3), .I4(in_4), .S(in_5), .C(CLK_out), .out_7(AL_out_7), .out_8(AL_out_8),
    .out_9(AL_out_9), .out_10(AL_out_10));
  fourbitregister AH (
    .I1(in_6), .I2(in_7), .I3(in_8), .I4(in_9), .S(in_10), .C(CLK_out), .out_7(AH_out_7), .out_8(AH_out_8),
    .out_9(AH_out_9), .out_10(AH_out_10));
  fourbitregister BL (
    .I1(in_11), .I2(in_12), .I3(in_13), .I4(in_14), .S(in_15), .C(CLK_out), .out_7(BL_out_7),
    .out_8(BL_out_8), .out_9(BL_out_9), .out_10(BL_out_10));
  fourbitregister BH (
    .I1(in_16), .I2(in_17), .I3(in_18), .I4(in_19), .S(in_20), .C(CLK_out), .out_7(BH_out_7),
    .out_8(BH_out_8), .out_9(BH_out_9), .out_10(BH_out_10));
  fourbitregister IR (
    .I1(in_21), .I2(in_22), .I3(in_23), .I4(in_24), .S(in_25), .C(CLK_out), .out_7(IR_out_7),
    .out_8(IR_out_8), .out_9(IR_out_9), .out_10(IR_out_10));
  LED led_1 (.in(AL_out_7));
  LED led_2 (.in(AL_out_8));
  LED led_3 (.in(AL_out_9));
  LED led_4 (.in(AL_out_10));
  LED led_5 (.in(AH_out_7));
  LED led_6 (.in(AH_out_8));
  LED led_7 (.in(AH_out_9));
  LED led_8 (.in(AH_out_10));
  LED led_9 (.in(BL_out_7));
  LED led_10 (.in(BL_out_8));
  LED led_11 (.in(BL_out_9));
  LED led_12 (.in(BL_out_10));
  LED led_13 (.in(BH_out_7));
  LED led_14 (.in(BH_out_8));
  LED led_15 (.in(BH_out_9));
  LED led_16 (.in(BH_out_10));
  LED led_17 (.in(IR_out_7));
  LED led_18 (.in(IR_out_8));
  LED led_19 (.in(IR_out_9));
  LED led_20 (.in(IR_out_10));
endmodule

module halfadder (
  input  A,
  input  B,
  output SUM,
  output CARRY
);

  xor xor_1 (SUM, A, B);
  and and_1 (CARRY, A, B);
endmodule

module fulladder (
  input  CIN,
  input  A,
  input  B,
  output Sum,
  output Carry
);

  wire and_1_out, and_2_out, xor_1_out;

  xor xor_1 (xor_1_out, A, B);
  and and_1 (and_1_out, A, B);
  xor xor_2 (Sum, xor_1_out, CIN);
  and and_2 (and_2_out, CIN, xor_1_out);
  or or_1 (Carry, and_2_out, and_1_out);
endmodule

module fourbitadder (
  input  in_1,
  input  A1,
  input  A3,
  input  B1,
  input  B3,
  input  A2,
  input  A4,
  input  B2,
  input  B4,
  output out_10,
  output out_11,
  output out_12,
  output out_13,
  output out_14
);

  wire fulladder_1_carry, fulladder_2_carry, fulladder_3_carry;

  fulladder fulladder_1 (.CIN(in_1), .A(A1), .B(A3), .Sum(out_10), .Carry(fulladder_1_carry));
  fulladder fulladder_2 (.CIN(fulladder_1_carry), .A(B1), .B(B3), .Sum(out_11), .Carry(fulladder_2_carry));
  fulladder fulladder_3 (.CIN(fulladder_2_carry), .A(A2), .B(A4), .Sum(out_12), .Carry(fulladder_3_carry));
  fulladder fulladder_4 (.CIN(fulladder_3_carry), .A(B2), .B(B4), .Sum(out_13), .Carry(out_14));
endmodule

module srlatch (
  input  S,
  input  R,
  output Q
);

  wire nor_2_out;

  nor nor_1 (Q, nor_2_out, R);
  nor nor_2 (nor_2_out, S, Q);
endmodule

module DLATCH (
  input  D,
  input  S,
  output Q
);

  wire and_1_out, and_2_out, nor_2_out, not_1_out;

  not not_1 (not_1_out, D);
  and and_1 (and_1_out, D, S);
  and and_2 (and_2_out, S, not_1_out);
  nor nor_1 (Q, nor_2_out, and_2_out);
  nor nor_2 (nor_2_out, and_1_out, Q);
endmodule

module DFLP (
  input  D,
  input  C,
  output Q
);

  wire dlatch_1_q, not_1_out;

  not not_1 (not_1_out, C);
  DLATCH dlatch_1 (.D(D), .S(not_1_out), .Q(dlatch_1_q));
  DLATCH dlatch_2 (.D(dlatch_1_q), .S(C), .Q(Q));
endmodule

module obreg (
  input  D,
  input  S,
  input  C,
  output out_4
);

  wire and_1_out, and_2_out, not_1_out, or_1_out;

  not not_1 (not_1_out, S);
  and and_1 (and_1_out, out_4, not_1_out);
  and and_2 (and_2_out, S, D);
  or or_1 (or_1_out, and_1_out, and_2_out);
  DFLP dflp_1 (.D(or_1_out), .C(C), .Q(out_4));
endmodule

module fourbitregister (
  input  I1,
  input  I2,
  input  I3,
  input  I4,
  input  S,
  input  C,
  output out_7,
  output out_8,
  output out_9,
  output out_10
);

  obreg obreg_1 (.D(I1), .S(S), .C(C), .out_4(out_7));
  obreg obreg_2 (.D(I2), .S(S), .C(C), .out_4(out_8));
  obreg obreg_3 (.D(I4), .S(S), .C(C), .out_4(out_10));
  obreg obreg_4 (.D(I3), .S(S), .C(C), .out_4(out_9));
endmodule

module ALU (
  input  in_1,
  input  in_2,
  input  in_3,
  input  in_4,
  input  SIG,
  output out_6,
  output out_7,
  output out_8,
  output out_9
);

  ALUDecoder aludecoder_1 (
    .S1(in_1), .S2(in_2), .S3(in_3), .S4(in_4), .ADD(SIG), .R1(out_6), .R2(out_7), .R3(out_8), .R4(out_9));  // open: A1, A2, A4, A5
endmodule

module ALUDecoder (
  input  S1,
  input  S2,
  input  S3,
  input  S4,
  input  A1,
  input  A2,
  input  A4,
  input  A5,
  input  ADD,
  output R1,
  output R2,
  output R3,
  output R4
);

  Multiplexer multiplexer_1 (.in0(S1), .in1(A1), .out(R1), .sel(ADD));
  Multiplexer multiplexer_2 (.in0(S2), .in1(A2), .out(R2), .sel(ADD));
  Multiplexer multiplexer_3 (.in0(S3), .in1(A4), .out(R3), .sel(ADD));
  Multiplexer multiplexer_4 (.in0(S4), .in1(A5), .out(R4), .sel(ADD));
endmodule
